// Digital circuit U63_GAL22V10_AY_FE_Digital.dig as structural Verilog
module U63_GAL22V10_AY_FE_Digital (
  input  bA14,
  input  bA15,
  input  nIOWR,
  input  bnM1,
  input  bA0,
  input  bA1,
  input  bA2,
  input  bA3,
  input  bA4,
  input  bA5,
  input  bA6,
  input  bA7,
  output BDIR,
  output BC1,
  output _8255_CS
);

  wire _74138_1_pin12, _74138_1_pin13, nand_1_out, nand_2_out, not_1_out, not_2_out;

  not not_1 (not_1_out, bA0);
  not not_2 (not_2_out, bA5);
  nand nand_1 (nand_1_out, bA0, not_2_out);
  nand nand_2 (nand_2_out, not_1_out, bA1, bA2, bA3, bA4, bA5, bA6, bA7);
  and and_1 (_8255_CS, nand_1_out, nand_2_out);
  _74138 _74138_1 (
    .pin1(bA14), .pin2(bA15), .pin3(bA1), .pin4(1'b0), .pin5(nIOWR), .pin6(bnM1), .pin8(1'b0),
    .pin12(_74138_1_pin12), .pin13(_74138_1_pin13), .pin16(1'b1));  // open: pin7, pin9, pin10, pin11, pin14, pin15
  nand nand_3 (BDIR, _74138_1_pin13, _74138_1_pin12);
  nand nand_4 (BC1, _74138_1_pin12, _74138_1_pin12);

  // Notes on the sheet:
  //   bA14: pin 2
  //   bA15: pin 14
  //   nIOWR: pin 13
  //   bnM1: pin 15
  //   BDIR: pin 17
  //   BC1: pin 16
  //   bA0: pin 10
  //   bA1: pin 9
  //   bA2: pin 8
  //   bA3: pin 7
  //   bA4: pin 6
  //   bA5: pin 5
  //   bA6: pin 4
  //   bA7: pin 3
  //   _8255_CS: pin 18
endmodule
